# Fritzing sketch Liploft_Breadboard (saved by Fritzing 0.9.3b)
breadboards: 2

parts:
  Part1 = Arduino Micro (Rev3)
  Part2 = Bluetooth Mate Silver
  R1 = 5.6K Ω Resistor [package=THT]
  MCP1 = MCP4161 [package=dip08]
  MCP2 = MCP4161 [package=dip08]
  R2 = 5.6K Ω Resistor [package=THT]
  MCP3 = MCP4161 [package=dip08]
  MCP4 = MCP4161 [package=dip08]
  R3 = 5.6K Ω Resistor [package=THT]
  R4 = 5.6K Ω Resistor [package=THT]
  LED1 = LED - 5mm [color="Red (633nm)" package="5 mm [THT]"]
  R5 = Resistor [tolerance=±5% resistance=220 package="1206 [SMD]"]

nets:
  N1: Part1.MOSI, MCP1.PB3(CS), MCP2.PB3(CS), MCP3.PB3(CS), MCP4.PB3(CS)
  N2: Part1.D1/TX, Part2.RX_5V
  N3: Part1.D0/RX, Part2.TX_5V
  GND: Part1.GND, Part2.GND, MCP1.GND, MCP1.PB5(P0A), MCP2.GND, MCP2.PB5(P0A), MCP3.GND, MCP3.PB5(P0A), MCP4.GND, MCP4.PB5(P0A), LED1.cathode
  N4: Part1.D5_PWM, R5.Pin_0
  N5: Part1.D7, MCP1.PB1(SDI)
  N6: Part1.D8_PWM/A8, MCP2.PB1(SDI)
  N7: Part1.D9_PWM/A9, MCP4.PB1(SDI)
  N8: Part1.D10_PWM/A10, MCP3.PB1(SDI)
  N9: Part1.SCK, MCP1.PB2(SCK), MCP2.PB2(SCK), MCP3.PB2(SCK), MCP4.PB2(SCK)
  VCC: Part1.5V, Part2.VCC, R1.Pin_1, MCP1.VCC, MCP2.VCC, R2.Pin_1, MCP3.VCC, MCP4.VCC, R3.Pin_1, R4.Pin_1
  N10: Part2.RTS_5V, Part2.CTS_5V
  N11: R1.Pin_0, MCP1.PB6(P0W), MCP1.PB7(P0B)
  N12: MCP2.PB6(P0W), MCP2.PB7(P0B), R2.Pin_0
  N13: MCP3.PB6(P0W), MCP3.PB7(P0B), R3.Pin_0
  N14: MCP4.PB6(P0W), MCP4.PB7(P0B), R4.Pin_0
  N15: LED1.anode, R5.Pin_1

custom parts:
  5.6K Ω Resistor: A generic resistor (0.25W)
  MCP4161: Digital Potentiometer
